# Fritzing sketch Motion activated rgb adressable strip (saved by Fritzing 0.9.10b)
circuit board: 23.815cm x 8.55882cm

parts:
  Gizwits_WiFi_Witty_ESP-12F1 = Gizwits WiFi Witty ESP-12F
  PIR1 = PIR sensor
  PIR2 = PIR sensor
  U2 = WS2812 RGB LED strip
  U3 = WS2812 RGB LED strip
  YwRobot_Power_Supply1 = YwRobot Breadboard Power Supply [part_number=545043]

nets (from the pcb view):
  VCC: Gizwits_WiFi_Witty_ESP-12F1.VCC, PIR1.VDD, PIR2.VDD, U2.VCC#1, YwRobot_Power_Supply1.VCC
  GND: Gizwits_WiFi_Witty_ESP-12F1.GND, PIR1.GND, PIR2.GND
  N1: Gizwits_WiFi_Witty_ESP-12F1.GPIO15, PIR1.SIG, PIR2.SIG, U2.GND#0, YwRobot_Power_Supply1.GND
  N2: Gizwits_WiFi_Witty_ESP-12F1.GPIO2, U2.DIN
  N3: U2.GND#4, U3.GND
  N4: U2.VCC#5, U3.VCC
  N5: U2.DOUT, U3.DIN

custom parts:
  WS2812 RGB LED strip: WS2812 strip
  YwRobot Breadboard Power Supply: The YwRobot Breadboard Power Supply (MB-V2) has two power rails; they can be 5V or 3V3. Power to the module can be provided through the female USB socket or through the A10 (female) 2.1mm power jack.
